# Fritzing sketch laserdriver (saved by Fritzing 0.8.3b)
breadboards: 1

parts:
  J1 = Basic Servo
  J3 = Basic Servo
  Q1 = NPN-Transistor [package="TO92 [THT]"]
  R1 = Resistor [tolerance=±5% resistance=200 package=THT]
  LED1 = smd LED [color="Red (633nm)" package="1206 [SMD]"]
  Parte1 = Arduino Uno (Rev3)
  R2 = Rotary Potentiometer (Small)
  U1 = V_REG_MIC2920 [package=sot223]
  VCC1 = Battery
  VCC3 = Battery  # not connected
  VCC5 = Battery

nets:
  N1: J1.pulse, Parte1.D9_PWM
  N2: J3.pulse, Parte1.D8
  N3: Q1.E, Parte1.GND, R2.leg2, U1.OUT
  N4: Q1.B, R1.Pin_1
  N5: Q1.C, LED1.anode
  N6: R1.Pin_0, Parte1.D10_PWM/SS
  N7: LED1.cathode, Parte1.5V, R2.leg1
  N8: Parte1.A0, R2.wiper
  N9: U1.IN, VCC1.+
  N10: U1.GND, VCC5.-
